// Logisim project Circuitos.circ as structural Verilog
module Ejercicio_02 (
  input  C_in,
  input  A,
  input  B,
  output O,
  output C_out
);

  wire and_1_out, and_2_out, xor_1_out;

  xor xor_1 (xor_1_out, A, B);
  and and_1 (and_1_out, B, A);
  xor xor_2 (O, C_in, xor_1_out);
  and and_2 (and_2_out, xor_1_out, C_in);
  or or_1 (C_out, and_1_out, and_2_out);
endmodule

module Ejercicio_03 (
  input  [7:0] A,
  input  [7:0] B,
  output [7:0] Resultado,
  output out_4
);

  wire Sumador_1_c_out, Sumador_2_c_out, Sumador_3_c_out, Sumador_4_c_out, Sumador_5_c_out, Sumador_6_c_out,
       Sumador_7_c_out;

  Ejercicio_02 Sumador_1 (.C_in(1'b0), .A(A[0]), .B(B[0]), .O(Resultado[0]), .C_out(Sumador_1_c_out));
  Ejercicio_02 Sumador_2 (.C_in(Sumador_1_c_out), .A(A[1]), .B(B[1]), .O(Resultado[1]), .C_out(Sumador_2_c_out));
  Ejercicio_02 Sumador_3 (.C_in(Sumador_2_c_out), .A(A[2]), .B(B[2]), .O(Resultado[2]), .C_out(Sumador_3_c_out));
  Ejercicio_02 Sumador_4 (.C_in(Sumador_3_c_out), .A(A[3]), .B(B[3]), .O(Resultado[3]), .C_out(Sumador_4_c_out));
  Ejercicio_02 Sumador_5 (.C_in(Sumador_4_c_out), .A(A[4]), .B(B[4]), .O(Resultado[4]), .C_out(Sumador_5_c_out));
  Ejercicio_02 Sumador_6 (.C_in(Sumador_5_c_out), .A(A[5]), .B(B[5]), .O(Resultado[5]), .C_out(Sumador_6_c_out));
  Ejercicio_02 Sumador_7 (.C_in(Sumador_6_c_out), .A(A[6]), .B(B[6]), .O(Resultado[6]), .C_out(Sumador_7_c_out));
  Ejercicio_02 Sumador_8 (.C_in(Sumador_7_c_out), .A(A[7]), .B(B[7]), .O(Resultado[7]), .C_out(out_4));
endmodule
